# Fritzing sketch Decibelimetro (saved by Fritzing 0.9.3b)
breadboards: 1

parts:
  LCD1 = LCD screen
  LCM1602_IIC1 = LCM1602 IIC [part_number="LCM1602 IIC" chip_label="LCM1602 IIC" package="DIP (Dual Inline) [THT]"]
  Part2 = KY-037 High Sensitivity Sound Detection Module [package="Breakout board"]
  Part3 = Arduino Mega 2560 (Rev3)
  U1 = NodeMCU V3.0

nets:
  VSS: LCD1.VSS, LCM1602_IIC1.VSS
  VDD: LCD1.VDD, LCM1602_IIC1.VDD
  N1: LCD1.V0, LCM1602_IIC1.V0
  N2: LCD1.RS, LCM1602_IIC1.RS
  N3: LCD1.R/W, LCM1602_IIC1.RW
  N4: LCD1.E, LCM1602_IIC1.E
  N5: LCD1.DB0, LCM1602_IIC1.D0
  N6: LCD1.DB1, LCM1602_IIC1.D1
  N7: LCD1.DB2, LCM1602_IIC1.D2
  N8: LCD1.DB3, LCM1602_IIC1.D3
  N9: LCD1.DB4, LCM1602_IIC1.D4
  N10: LCD1.DB5, LCM1602_IIC1.D5
  N11: LCD1.DB6, LCM1602_IIC1.D6
  N12: LCD1.DB7, LCM1602_IIC1.D7
  N13: LCD1.LED+, LCM1602_IIC1.A
  N14: LCD1.LED-, LCM1602_IIC1.K
  GND: LCM1602_IIC1.GND, Part2.G, Part3.GND, U1.GND
  VCC: LCM1602_IIC1.VCC, Part2.+, Part3.5V
  N15: LCM1602_IIC1.SDA, Part3.D20/SDA
  N16: LCM1602_IIC1.SCL, Part3.D21/SCL
  N17: Part2.A0, Part3.A0
  N18: Part3.D19/RX1, U1.TX
  N19: Part3.D18/TX1, U1.RX
  3V3: Part3.3V3, U1.3V3

custom parts:
  LCM1602 IIC: I2C-Module to use a 1602 or 2004 LCD on with the wire.h libory Serial LCD Modul
  KY-037 High Sensitivity Sound Detection Module: KY-037 high sensitivity sound detection module is an analog/digital sensor that uses a condenser microphone to observe changes in environment noise.
  NodeMCU V3.0: ESP8266 based NodeMCU
